// Logisim project circuit.circ as structural Verilog: 17 circuits, main circuit four_bit_full_adder_without_enable
module main (
  input  carry_in
);

  wire and_1_out, and_2_out, and_3_out, and_4_out, and_5_out, and_6_out, and_7_out, controlled_buffer_1_out,
       controlled_buffer_2_out, controlled_buffer_3_out, controlled_buffer_4_out, decoder_1_out0,
       decoder_1_out1, decoder_1_out2, decoder_1_out3, decoder_2_out0, decoder_2_out1, decoder_2_out2,
       decoder_2_out3, decoder_2_out4, decoder_2_out5, decoder_2_out6, decoder_2_out7,
       four_bit_full_adder_1_carry_out, four_bit_multiplier_1_s4, four_bit_multiplier_1_s5,
       four_bit_multiplier_1_s6, four_bit_multiplier_1_s7, input_a_p1, input_a_p2, input_a_p3, input_a_p4,
       input_b_p1, input_b_p2, input_b_p3, input_b_p4, or_1_out;
  wire [1:0] screen_p2;
  wire [2:0] opcode_p3;
  wire [3:0] double_dabble_1_h0, double_dabble_1_o0, double_dabble_1_t0;

  // DipSwitch #(.number(2)) screen: pin names not known; wires that end beside it: screen_p2[1], screen_p2[0]
  Decoder #(.enable("false"), .select(2)) decoder_1 (
    .out0(decoder_1_out0), .out1(decoder_1_out1), .out2(decoder_1_out2), .out3(decoder_1_out3),
    .sel(screen_p2));
  // DipSwitch #(.number(3)) opcode: pin names not known; wires that end beside it: opcode_p3[2], opcode_p3[1], opcode_p3[0]
  Decoder #(.enable("false"), .select(3)) decoder_2 (
    .out0(decoder_2_out0), .out1(decoder_2_out1), .out2(decoder_2_out2), .out3(decoder_2_out3),
    .out4(decoder_2_out4), .out5(decoder_2_out5), .out6(decoder_2_out6), .out7(decoder_2_out7),
    .sel(opcode_p3));
  LED error (.in(or_1_out));
  or or_1 (or_1_out, decoder_2_out6, decoder_2_out7);
  assign controlled_buffer_1_out = decoder_1_out0 ? opcode_p3[2] : 1'bz;  // Controlled_Buffer controlled_buffer_1
  assign controlled_buffer_2_out = decoder_1_out0 ? opcode_p3[1] : 1'bz;  // Controlled_Buffer controlled_buffer_2
  assign controlled_buffer_3_out = decoder_1_out0 ? opcode_p3[0] : 1'bz;  // Controlled_Buffer controlled_buffer_3
  and and_1 (and_1_out, decoder_2_out0, decoder_1_out3);
  and and_2 (and_2_out, decoder_2_out1, decoder_1_out3);
  and and_3 (and_3_out, decoder_2_out2, decoder_1_out3);
  and and_4 (and_4_out, decoder_2_out3, decoder_1_out3);
  and and_5 (and_5_out, decoder_2_out4, decoder_1_out3);
  and and_6 (and_6_out, decoder_2_out5, decoder_1_out3);
  // DipSwitch #(.number(4)) input_a: pin names not known; wires that end beside it: input_a_p1, input_a_p2, input_a_p3, input_a_p4
  assign controlled_buffer_4_out = decoder_1_out1 ? input_a_p1 : 1'bz;  // Controlled_Buffer controlled_buffer_4
  assign controlled_buffer_1_out = decoder_1_out1 ? input_a_p2 : 1'bz;  // Controlled_Buffer controlled_buffer_5
  assign controlled_buffer_2_out = decoder_1_out1 ? input_a_p3 : 1'bz;  // Controlled_Buffer controlled_buffer_6
  assign controlled_buffer_3_out = decoder_1_out1 ? input_a_p4 : 1'bz;  // Controlled_Buffer controlled_buffer_7
  // DipSwitch #(.number(4)) input_b: pin names not known; wires that end beside it: input_b_p1, input_b_p2, input_b_p3, input_b_p4
  assign controlled_buffer_4_out = decoder_1_out2 ? input_b_p1 : 1'bz;  // Controlled_Buffer controlled_buffer_8
  assign controlled_buffer_1_out = decoder_1_out2 ? input_b_p2 : 1'bz;  // Controlled_Buffer controlled_buffer_9
  assign controlled_buffer_2_out = decoder_1_out2 ? input_b_p3 : 1'bz;  // Controlled_Buffer controlled_buffer_10
  assign controlled_buffer_3_out = decoder_1_out2 ? input_b_p4 : 1'bz;  // Controlled_Buffer controlled_buffer_11
  LED led_1 (.in(carry_in));
  double_dabble double_dabble_1 (
    .a(four_bit_multiplier_1_s7), .b(four_bit_multiplier_1_s6), .c(four_bit_multiplier_1_s5),
    .d(four_bit_multiplier_1_s4), .e(controlled_buffer_4_out), .f(controlled_buffer_1_out),
    .g(controlled_buffer_2_out), .h(controlled_buffer_3_out), .h3(double_dabble_1_h0[3]),
    .h2(double_dabble_1_h0[2]), .h1(double_dabble_1_h0[1]), .h0(double_dabble_1_h0[0]),
    .t3(double_dabble_1_t0[3]), .t2(double_dabble_1_t0[2]), .t1(double_dabble_1_t0[1]),
    .t0(double_dabble_1_t0[0]), .o3(double_dabble_1_o0[3]), .o2(double_dabble_1_o0[2]),
    .o1(double_dabble_1_o0[1]), .o0(double_dabble_1_o0[0]));
  _7_Segment_Display u_7_segment_display_1 ();  // open: g, f, a, b, e, d, c, dp
  _7_Segment_Display u_7_segment_display_2 ();  // open: g, f, a, b, e, d, c, dp
  // BCD_to_7_Segment_decoder bcd_to_7_segment_decoder_1: pin names not known
  // BCD_to_7_Segment_decoder bcd_to_7_segment_decoder_2: pin names not known
  _7_Segment_Display u_7_segment_display_3 ();  // open: g, f, a, b, e, d, c, dp
  // BCD_to_7_Segment_decoder bcd_to_7_segment_decoder_3: pin names not known
  LED carry_out (.in(four_bit_full_adder_1_carry_out));
  LED overflow (.in(and_7_out));
  and and_7 (and_7_out, four_bit_full_adder_1_carry_out, and_1_out);
  four_bit_full_adder four_bit_full_adder_1 (
    .enable(and_1_out), .a0(input_a_p4), .b0(input_b_p4), .carry_in(carry_in), .a1(input_a_p3),
    .b1(input_b_p3), .a2(input_a_p2), .b2(input_b_p2), .a3(input_a_p1), .b3(input_b_p1),
    .s0(controlled_buffer_3_out), .s1(controlled_buffer_2_out), .s2(controlled_buffer_1_out),
    .s3(controlled_buffer_4_out), .carry_out(four_bit_full_adder_1_carry_out));
  four_bit_full_subtractor four_bit_full_subtractor_1 (
    .enable(and_2_out), .a0(input_a_p4), .b0(input_b_p4), .borrow_in(carry_in), .a1(input_a_p3),
    .b1(input_b_p3), .a2(input_a_p2), .b2(input_b_p2), .a3(input_a_p1), .b3(input_b_p1),
    .s0(controlled_buffer_3_out), .s1(controlled_buffer_2_out), .s2(controlled_buffer_1_out),
    .s3(controlled_buffer_4_out), .borrow_out(four_bit_full_adder_1_carry_out));
  four_bit_multiplier four_bit_multiplier_1 (
    .enable(and_3_out), .a0(input_a_p4), .a1(input_a_p3), .a2(input_a_p2), .a3(input_a_p1), .b0(input_b_p4),
    .b1(input_b_p3), .b2(input_b_p2), .b3(input_b_p1), .s0(controlled_buffer_3_out),
    .s1(controlled_buffer_2_out), .s2(controlled_buffer_1_out), .s3(controlled_buffer_4_out),
    .s4(four_bit_multiplier_1_s4), .s5(four_bit_multiplier_1_s5), .s6(four_bit_multiplier_1_s6),
    .s7(four_bit_multiplier_1_s7));
  four_bit_and four_bit_and_1 (
    .a0(input_a_p4), .enable(and_4_out), .b0(input_b_p4), .a1(input_a_p3), .b1(input_b_p3), .a2(input_a_p2),
    .b2(input_b_p2), .a3(input_a_p1), .b3(input_b_p1), .s0(controlled_buffer_3_out),
    .s1(controlled_buffer_2_out), .s2(controlled_buffer_1_out), .s3(controlled_buffer_4_out));
  four_bit_or four_bit_or_1 (
    .a0(input_a_p4), .enable(and_5_out), .b0(input_b_p4), .a1(input_a_p3), .b1(input_b_p3), .a2(input_a_p2),
    .b2(input_b_p2), .a3(input_a_p1), .b3(input_b_p1), .s0(controlled_buffer_3_out),
    .s1(controlled_buffer_2_out), .s2(controlled_buffer_1_out), .s3(controlled_buffer_4_out));
  four_bit_xor four_bit_xor_1 (
    .a0(input_a_p4), .enable(and_6_out), .b0(input_b_p4), .a1(input_a_p3), .b1(input_b_p3), .a2(input_a_p2),
    .b2(input_b_p2), .a3(input_a_p1), .b3(input_b_p1), .s0(controlled_buffer_3_out),
    .s1(controlled_buffer_2_out), .s2(controlled_buffer_1_out), .s3(controlled_buffer_4_out));
endmodule

module four_bit_and (
  input  a0,
  input  enable,
  input  b0,
  input  a1,
  input  b1,
  input  a2,
  input  b2,
  input  a3,
  input  b3,
  output s0,
  output s1,
  output s2,
  output s3
);

  wire and_1_out, and_2_out, and_3_out, and_4_out;

  and and_1 (and_1_out, a0, b0);
  and and_2 (and_2_out, a1, b1);
  and and_3 (and_3_out, a2, b2);
  and and_4 (and_4_out, a3, b3);
  assign s0 = enable ? and_1_out : 1'bz;  // Controlled_Buffer controlled_buffer_1
  assign s1 = enable ? and_2_out : 1'bz;  // Controlled_Buffer controlled_buffer_2
  assign s2 = enable ? and_3_out : 1'bz;  // Controlled_Buffer controlled_buffer_3
  assign s3 = enable ? and_4_out : 1'bz;  // Controlled_Buffer controlled_buffer_4
endmodule

module four_bit_or (
  input  a0,
  input  enable,
  input  b0,
  input  a1,
  input  b1,
  input  a2,
  input  b2,
  input  a3,
  input  b3,
  output s0,
  output s1,
  output s2,
  output s3
);

  wire or_1_out, or_2_out, or_3_out, or_4_out;

  or or_1 (or_1_out, a0, b0);
  or or_2 (or_2_out, a1, b1);
  or or_3 (or_3_out, a2, b2);
  or or_4 (or_4_out, a3, b3);
  assign s0 = enable ? or_1_out : 1'bz;  // Controlled_Buffer controlled_buffer_1
  assign s1 = enable ? or_2_out : 1'bz;  // Controlled_Buffer controlled_buffer_2
  assign s2 = enable ? or_3_out : 1'bz;  // Controlled_Buffer controlled_buffer_3
  assign s3 = enable ? or_4_out : 1'bz;  // Controlled_Buffer controlled_buffer_4
endmodule

module four_bit_xor (
  input  a0,
  input  enable,
  input  b0,
  input  a1,
  input  b1,
  input  a2,
  input  b2,
  input  a3,
  input  b3,
  output s0,
  output s1,
  output s2,
  output s3
);

  wire xor_1_out, xor_2_out, xor_3_out, xor_4_out;

  xor xor_1 (xor_1_out, a0, b0);
  xor xor_2 (xor_2_out, a1, b1);
  xor xor_3 (xor_3_out, a2, b2);
  xor xor_4 (xor_4_out, a3, b3);
  assign s0 = enable ? xor_1_out : 1'bz;  // Controlled_Buffer controlled_buffer_1
  assign s1 = enable ? xor_2_out : 1'bz;  // Controlled_Buffer controlled_buffer_2
  assign s2 = enable ? xor_3_out : 1'bz;  // Controlled_Buffer controlled_buffer_3
  assign s3 = enable ? xor_4_out : 1'bz;  // Controlled_Buffer controlled_buffer_4
endmodule

module four_bit_full_adder (
  input  enable,
  input  a0,
  input  b0,
  input  carry_in,
  input  a1,
  input  b1,
  input  a2,
  input  b2,
  input  a3,
  input  b3,
  output s0,
  output s1,
  output s2,
  output s3,
  output carry_out
);

  wire one_bit_full_adder_1_carry_out, one_bit_full_adder_1_s, one_bit_full_adder_2_carry_out,
       one_bit_full_adder_2_s, one_bit_full_adder_3_carry_out, one_bit_full_adder_3_s,
       one_bit_full_adder_4_carry_out, one_bit_full_adder_4_s;

  one_bit_full_adder one_bit_full_adder_1 (
    .a(a0), .b(b0), .carry_in(carry_in), .s(one_bit_full_adder_1_s),
    .carry_out(one_bit_full_adder_1_carry_out));
  one_bit_full_adder one_bit_full_adder_2 (
    .a(a1), .b(b1), .carry_in(one_bit_full_adder_1_carry_out), .s(one_bit_full_adder_2_s),
    .carry_out(one_bit_full_adder_2_carry_out));
  one_bit_full_adder one_bit_full_adder_3 (
    .a(a2), .b(b2), .carry_in(one_bit_full_adder_2_carry_out), .s(one_bit_full_adder_3_s),
    .carry_out(one_bit_full_adder_3_carry_out));
  one_bit_full_adder one_bit_full_adder_4 (
    .a(a3), .b(b3), .carry_in(one_bit_full_adder_3_carry_out), .s(one_bit_full_adder_4_s),
    .carry_out(one_bit_full_adder_4_carry_out));
  assign s0 = enable ? one_bit_full_adder_1_s : 1'bz;  // Controlled_Buffer controlled_buffer_1
  assign s1 = enable ? one_bit_full_adder_2_s : 1'bz;  // Controlled_Buffer controlled_buffer_2
  assign s2 = enable ? one_bit_full_adder_3_s : 1'bz;  // Controlled_Buffer controlled_buffer_3
  assign s3 = enable ? one_bit_full_adder_4_s : 1'bz;  // Controlled_Buffer controlled_buffer_4
  assign carry_out = enable ? one_bit_full_adder_4_carry_out : 1'bz;  // Controlled_Buffer controlled_buffer_5
endmodule

module four_bit_full_subtractor (
  input  enable,
  input  a0,
  input  b0,
  input  borrow_in,
  input  a1,
  input  b1,
  input  a2,
  input  b2,
  input  a3,
  input  b3,
  output s0,
  output s1,
  output s2,
  output s3,
  output borrow_out
);

  wire one_bit_full_subtractor_1_borrow_out, one_bit_full_subtractor_1_s,
       one_bit_full_subtractor_2_borrow_out, one_bit_full_subtractor_2_s,
       one_bit_full_subtractor_3_borrow_out, one_bit_full_subtractor_3_s,
       one_bit_full_subtractor_4_borrow_out, one_bit_full_subtractor_4_s;

  one_bit_full_subtractor one_bit_full_subtractor_1 (
    .a(a0), .b(b0), .borrow_in(borrow_in), .s(one_bit_full_subtractor_1_s),
    .borrow_out(one_bit_full_subtractor_1_borrow_out));
  one_bit_full_subtractor one_bit_full_subtractor_2 (
    .a(a1), .b(b1), .borrow_in(one_bit_full_subtractor_1_borrow_out), .s(one_bit_full_subtractor_2_s),
    .borrow_out(one_bit_full_subtractor_2_borrow_out));
  one_bit_full_subtractor one_bit_full_subtractor_3 (
    .a(a2), .b(b2), .borrow_in(one_bit_full_subtractor_2_borrow_out), .s(one_bit_full_subtractor_3_s),
    .borrow_out(one_bit_full_subtractor_3_borrow_out));
  one_bit_full_subtractor one_bit_full_subtractor_4 (
    .a(a3), .b(b3), .borrow_in(one_bit_full_subtractor_3_borrow_out), .s(one_bit_full_subtractor_4_s),
    .borrow_out(one_bit_full_subtractor_4_borrow_out));
  assign s0 = enable ? one_bit_full_subtractor_1_s : 1'bz;  // Controlled_Buffer controlled_buffer_1
  assign s1 = enable ? one_bit_full_subtractor_2_s : 1'bz;  // Controlled_Buffer controlled_buffer_2
  assign s2 = enable ? one_bit_full_subtractor_3_s : 1'bz;  // Controlled_Buffer controlled_buffer_3
  assign s3 = enable ? one_bit_full_subtractor_4_s : 1'bz;  // Controlled_Buffer controlled_buffer_4
  assign borrow_out = enable ? one_bit_full_subtractor_4_borrow_out : 1'bz;  // Controlled_Buffer controlled_buffer_5
endmodule

module one_bit_full_adder (
  input  a,
  input  b,
  input  carry_in,
  output s,
  output carry_out
);

  wire one_bit_half_adder_1_carry_out, one_bit_half_adder_1_s, one_bit_half_adder_2_carry_out;

  one_bit_half_adder one_bit_half_adder_1 (
    .a(a), .b(b), .s(one_bit_half_adder_1_s), .carry_out(one_bit_half_adder_1_carry_out));
  one_bit_half_adder one_bit_half_adder_2 (
    .a(one_bit_half_adder_1_s), .b(carry_in), .s(s), .carry_out(one_bit_half_adder_2_carry_out));
  or or_1 (carry_out, one_bit_half_adder_1_carry_out, one_bit_half_adder_2_carry_out);
endmodule

module one_bit_full_subtractor (
  input  a,
  input  b,
  input  borrow_in,
  output s,
  output borrow_out
);

  wire and_1_out, and_2_out, not_1_out, not_2_out, xor_1_out;

  xor xor_1 (xor_1_out, a, b);
  not not_1 (not_1_out, a);
  xor xor_2 (s, xor_1_out, borrow_in);
  not not_2 (not_2_out, xor_1_out);
  and and_1 (and_1_out, not_1_out, b);
  and and_2 (and_2_out, borrow_in, not_2_out);
  or or_1 (borrow_out, and_2_out, and_1_out);
endmodule

module one_bit_half_adder (
  input  a,
  input  b,
  output s,
  output carry_out
);

  xor xor_1 (s, a, b);
  and and_1 (carry_out, a, b);
endmodule

module two_bit_full_adder (
  input  a0,
  input  b0,
  input  carry_in,
  input  a1,
  input  b1,
  output s0,
  output s1,
  output carry_out
);

  wire one_bit_full_adder_1_carry_out;

  one_bit_full_adder one_bit_full_adder_1 (
    .a(a0), .b(b0), .carry_in(carry_in), .s(s0), .carry_out(one_bit_full_adder_1_carry_out));
  one_bit_full_adder one_bit_full_adder_2 (
    .a(a1), .b(b1), .carry_in(one_bit_full_adder_1_carry_out), .s(s1), .carry_out(carry_out));
endmodule

module three_bit_full_adder (
  input  a0,
  input  b0,
  input  carry_in,
  input  a1,
  input  b1,
  input  a2,
  input  b2,
  output s0,
  output s1,
  output s2,
  output carry_out
);

  wire one_bit_full_adder_1_carry_out;

  one_bit_full_adder one_bit_full_adder_1 (
    .a(a0), .b(b0), .carry_in(carry_in), .s(s0), .carry_out(one_bit_full_adder_1_carry_out));
  two_bit_full_adder two_bit_full_adder_1 (
    .a0(a1), .b0(b1), .carry_in(one_bit_full_adder_1_carry_out), .a1(a2), .b1(b2), .s0(s1), .s1(s2),
    .carry_out(carry_out));
endmodule

module four_bit_multiplier (
  input  enable,
  input  a0,
  input  a1,
  input  a2,
  input  a3,
  input  b0,
  input  b1,
  input  b2,
  input  b3,
  output s0,
  output s1,
  output s2,
  output s3,
  output s4,
  output s5,
  output s6,
  output s7
);

  wire a0b0_out, a0b1_out, a0b2_out, a0b3_out, a1b0_out, a1b1_out, a1b2_out, a1b3_out, a2b0_out, a2b1_out,
       a2b2_out, a2b3_out, a3b0_out, a3b1_out, a3b2_out, a3b3_out, one_bit_half_adder_1_carry_out,
       one_bit_half_adder_1_s, one_bit_half_adder_2_carry_out, one_bit_half_adder_2_s,
       one_bit_half_adder_3_carry_out, one_bit_half_adder_3_s, one_bit_half_adder_4_carry_out,
       one_bit_half_adder_4_s, three_bit_full_adder_1_carry_out, three_bit_full_adder_1_s0,
       three_bit_full_adder_1_s1, three_bit_full_adder_1_s2, three_bit_full_adder_2_carry_out,
       three_bit_full_adder_2_s0, three_bit_full_adder_2_s1, three_bit_full_adder_2_s2,
       two_bit_full_adder_1_carry_out, two_bit_full_adder_1_s0, two_bit_full_adder_1_s1;

  and a0b0 (a0b0_out, a0, b0);
  and a1b0 (a1b0_out, a1, b0);
  and a2b0 (a2b0_out, a2, b0);
  and a3b0 (a3b0_out, a3, b0);
  and a0b1 (a0b1_out, a0, b1);
  and a1b1 (a1b1_out, a1, b1);
  and a2b1 (a2b1_out, a2, b1);
  and a3b1 (a3b1_out, a3, b1);
  one_bit_half_adder one_bit_half_adder_1 (
    .a(a1b0_out), .b(a0b1_out), .s(one_bit_half_adder_1_s), .carry_out(one_bit_half_adder_1_carry_out));
  two_bit_full_adder two_bit_full_adder_1 (
    .a0(a2b0_out), .b0(a1b1_out), .carry_in(one_bit_half_adder_1_carry_out), .a1(a3b0_out), .b1(a2b1_out),
    .s0(two_bit_full_adder_1_s0), .s1(two_bit_full_adder_1_s1), .carry_out(two_bit_full_adder_1_carry_out));
  one_bit_half_adder one_bit_half_adder_2 (
    .a(two_bit_full_adder_1_carry_out), .b(a3b1_out), .s(one_bit_half_adder_2_s),
    .carry_out(one_bit_half_adder_2_carry_out));
  and a0b2 (a0b2_out, a0, b2);
  and a1b2 (a1b2_out, a1, b2);
  and a2b2 (a2b2_out, a2, b2);
  and a3b2 (a3b2_out, a3, b2);
  one_bit_half_adder one_bit_half_adder_3 (
    .a(two_bit_full_adder_1_s0), .b(a0b2_out), .s(one_bit_half_adder_3_s),
    .carry_out(one_bit_half_adder_3_carry_out));
  three_bit_full_adder three_bit_full_adder_1 (
    .a0(a1b2_out), .b0(two_bit_full_adder_1_s1), .carry_in(one_bit_half_adder_3_carry_out), .a1(a2b2_out),
    .b1(one_bit_half_adder_2_s), .a2(one_bit_half_adder_2_carry_out), .b2(a3b2_out),
    .s0(three_bit_full_adder_1_s0), .s1(three_bit_full_adder_1_s1), .s2(three_bit_full_adder_1_s2),
    .carry_out(three_bit_full_adder_1_carry_out));
  and a0b3 (a0b3_out, a0, b3);
  and a1b3 (a1b3_out, a1, b3);
  and a2b3 (a2b3_out, a2, b3);
  and a3b3 (a3b3_out, a3, b3);
  one_bit_half_adder one_bit_half_adder_4 (
    .a(a0b3_out), .b(three_bit_full_adder_1_s0), .s(one_bit_half_adder_4_s),
    .carry_out(one_bit_half_adder_4_carry_out));
  three_bit_full_adder three_bit_full_adder_2 (
    .a0(a1b3_out), .b0(three_bit_full_adder_1_s1), .carry_in(one_bit_half_adder_4_carry_out), .a1(a2b3_out),
    .b1(three_bit_full_adder_1_s2), .a2(three_bit_full_adder_1_carry_out), .b2(a3b3_out),
    .s0(three_bit_full_adder_2_s0), .s1(three_bit_full_adder_2_s1), .s2(three_bit_full_adder_2_s2),
    .carry_out(three_bit_full_adder_2_carry_out));
  assign s0 = enable ? a0b0_out : 1'bz;  // Controlled_Buffer controlled_buffer_1
  assign s1 = enable ? one_bit_half_adder_1_s : 1'bz;  // Controlled_Buffer controlled_buffer_2
  assign s2 = enable ? one_bit_half_adder_3_s : 1'bz;  // Controlled_Buffer controlled_buffer_3
  assign s3 = enable ? one_bit_half_adder_4_s : 1'bz;  // Controlled_Buffer controlled_buffer_4
  assign s4 = enable ? three_bit_full_adder_2_s0 : 1'bz;  // Controlled_Buffer controlled_buffer_5
  assign s5 = enable ? three_bit_full_adder_2_s1 : 1'bz;  // Controlled_Buffer controlled_buffer_6
  assign s6 = enable ? three_bit_full_adder_2_s2 : 1'bz;  // Controlled_Buffer controlled_buffer_7
  assign s7 = enable ? three_bit_full_adder_2_carry_out : 1'bz;  // Controlled_Buffer controlled_buffer_8
endmodule

module dabble (
  input  a,
  input  b,
  input  c,
  input  d,
  output e,
  output f,
  output g,
  output h
);

  wire nor_1_out, nor_2_out, or_1_out, xor_1_out, xor_2_out;

  xor xor_1 (xor_1_out, d, a);
  nor nor_1 (nor_1_out, a, b);
  xor xor_2 (xor_2_out, a, c);
  nor nor_2 (nor_2_out, xor_1_out, xor_2_out);
  nor nor_3 (e, nor_2_out, nor_1_out);
  or or_1 (or_1_out, xor_1_out, nor_1_out);
  nor nor_4 (f, c, or_1_out);
  and and_1 (g, xor_2_out, or_1_out);
  xor xor_3 (h, e, d);
endmodule

module double_dabble (
  input  a,
  input  b,
  input  c,
  input  d,
  input  e,
  input  f,
  input  g,
  input  h,
  output h3,
  output h2,
  output h1,
  output h0,
  output t3,
  output t2,
  output t1,
  output t0,
  output o3,
  output o2,
  output o1,
  output o0
);

  wire dabble_1_e, dabble_1_f, dabble_1_g, dabble_1_h, dabble_2_e, dabble_2_f, dabble_2_g, dabble_2_h,
       dabble_3_e, dabble_3_f, dabble_3_g, dabble_3_h, dabble_4_f, dabble_4_g, dabble_4_h, dabble_5_e,
       dabble_5_f, dabble_5_g, dabble_5_h;

  dabble dabble_1 (.a(1'b0), .b(a), .c(b), .d(c), .e(dabble_1_e), .f(dabble_1_f), .g(dabble_1_g), .h(dabble_1_h));
  dabble dabble_2 (
    .a(dabble_1_f), .b(dabble_1_g), .c(dabble_1_h), .d(d), .e(dabble_2_e), .f(dabble_2_f), .g(dabble_2_g),
    .h(dabble_2_h));
  dabble dabble_3 (
    .a(dabble_2_f), .b(dabble_2_g), .c(dabble_2_h), .d(e), .e(dabble_3_e), .f(dabble_3_f), .g(dabble_3_g),
    .h(dabble_3_h));
  dabble dabble_4 (
    .a(1'b0), .b(dabble_1_e), .c(dabble_2_e), .d(dabble_3_e), .e(h1), .f(dabble_4_f), .g(dabble_4_g),
    .h(dabble_4_h));
  dabble dabble_5 (
    .a(dabble_3_f), .b(dabble_3_g), .c(dabble_3_h), .d(f), .e(dabble_5_e), .f(dabble_5_f), .g(dabble_5_g),
    .h(dabble_5_h));
  dabble dabble_6 (.a(dabble_4_f), .b(dabble_4_g), .c(dabble_4_h), .d(dabble_5_e), .e(h0), .f(t3), .g(t2), .h(t1));
  dabble dabble_7 (.a(dabble_5_f), .b(dabble_5_g), .c(dabble_5_h), .d(g), .e(t0), .f(o3), .g(o2), .h(o1));

  assign h2 = 1'b0;
  assign h3 = 1'b0;
  assign o0 = h;
endmodule

module multiplier_four_bit (
  input  enable,
  input  a0,
  input  a1,
  input  a2,
  input  a3,
  input  b0,
  input  b1,
  input  b2,
  input  b3,
  output s0,
  output s1,
  output s2,
  output s3,
  output s4,
  output s5,
  output s6,
  output s7
);

  wire a0b0_out, a0b1_out, a0b2_out, a0b3_out, a1b0_out, a1b1_out, a1b2_out, a1b3_out, a2b0_out, a2b1_out,
       a2b2_out, a2b3_out, a3b0_out, a3b1_out, a3b2_out, a3b3_out,
       four_bit_full_adder_without_enable_1_carry_out, four_bit_full_adder_without_enable_1_s0,
       four_bit_full_adder_without_enable_1_s1, four_bit_full_adder_without_enable_1_s2,
       four_bit_full_adder_without_enable_1_s3, four_bit_full_adder_without_enable_2_carry_out,
       four_bit_full_adder_without_enable_2_s0, four_bit_full_adder_without_enable_2_s1,
       four_bit_full_adder_without_enable_2_s2, four_bit_full_adder_without_enable_2_s3,
       four_bit_full_adder_without_enable_3_carry_out, four_bit_full_adder_without_enable_3_s0,
       four_bit_full_adder_without_enable_3_s1, four_bit_full_adder_without_enable_3_s2,
       four_bit_full_adder_without_enable_3_s3;

  and a0b0 (a0b0_out, a0, b0);
  and a1b0 (a1b0_out, a1, b0);
  and a2b0 (a2b0_out, a2, b0);
  and a3b0 (a3b0_out, a3, b0);
  and a0b1 (a0b1_out, a0, b1);
  and a1b1 (a1b1_out, a1, b1);
  and a2b1 (a2b1_out, a2, b1);
  and a3b1 (a3b1_out, a3, b1);
  four_bit_full_adder_without_enable four_bit_full_adder_without_enable_1 (
    .a0(a0b1_out), .b0(a1b0_out), .carry_in(1'b0), .a1(a1b1_out), .b1(a2b0_out), .a2(a2b1_out),
    .b2(a3b0_out), .a3(a3b1_out), .b3(1'b0), .s0(four_bit_full_adder_without_enable_1_s0),
    .s1(four_bit_full_adder_without_enable_1_s1), .s2(four_bit_full_adder_without_enable_1_s2),
    .s3(four_bit_full_adder_without_enable_1_s3), .carry_out(four_bit_full_adder_without_enable_1_carry_out));
  and a0b2 (a0b2_out, a0, b2);
  and a1b2 (a1b2_out, a1, b2);
  and a2b2 (a2b2_out, a2, b2);
  and a3b2 (a3b2_out, a3, b2);
  four_bit_full_adder_without_enable four_bit_full_adder_without_enable_2 (
    .a0(a0b2_out), .b0(four_bit_full_adder_without_enable_1_s1), .carry_in(1'b0), .a1(a1b2_out),
    .b1(four_bit_full_adder_without_enable_1_s2), .a2(a2b2_out),
    .b2(four_bit_full_adder_without_enable_1_s3), .a3(a3b2_out),
    .b3(four_bit_full_adder_without_enable_1_carry_out), .s0(four_bit_full_adder_without_enable_2_s0),
    .s1(four_bit_full_adder_without_enable_2_s1), .s2(four_bit_full_adder_without_enable_2_s2),
    .s3(four_bit_full_adder_without_enable_2_s3), .carry_out(four_bit_full_adder_without_enable_2_carry_out));
  and a0b3 (a0b3_out, a0, b3);
  and a1b3 (a1b3_out, a1, b3);
  and a2b3 (a2b3_out, a2, b3);
  and a3b3 (a3b3_out, a3, b3);
  four_bit_full_adder_without_enable four_bit_full_adder_without_enable_3 (
    .a0(a0b3_out), .b0(four_bit_full_adder_without_enable_2_s1), .carry_in(1'b0), .a1(a1b3_out),
    .b1(four_bit_full_adder_without_enable_2_s2), .a2(a2b3_out),
    .b2(four_bit_full_adder_without_enable_2_s3), .a3(a3b3_out),
    .b3(four_bit_full_adder_without_enable_2_carry_out), .s0(four_bit_full_adder_without_enable_3_s0),
    .s1(four_bit_full_adder_without_enable_3_s1), .s2(four_bit_full_adder_without_enable_3_s2),
    .s3(four_bit_full_adder_without_enable_3_s3), .carry_out(four_bit_full_adder_without_enable_3_carry_out));
  assign s0 = enable ? a0b0_out : 1'bz;  // Controlled_Buffer controlled_buffer_1
  assign s1 = enable ? four_bit_full_adder_without_enable_1_s0 : 1'bz;  // Controlled_Buffer controlled_buffer_2
  assign s2 = enable ? four_bit_full_adder_without_enable_2_s0 : 1'bz;  // Controlled_Buffer controlled_buffer_3
  assign s3 = enable ? four_bit_full_adder_without_enable_3_s0 : 1'bz;  // Controlled_Buffer controlled_buffer_4
  assign s4 = enable ? four_bit_full_adder_without_enable_3_s1 : 1'bz;  // Controlled_Buffer controlled_buffer_5
  assign s5 = enable ? four_bit_full_adder_without_enable_3_s2 : 1'bz;  // Controlled_Buffer controlled_buffer_6
  assign s6 = enable ? four_bit_full_adder_without_enable_3_s3 : 1'bz;  // Controlled_Buffer controlled_buffer_7
  assign s7 = enable ? four_bit_full_adder_without_enable_3_carry_out : 1'bz;  // Controlled_Buffer controlled_buffer_8
endmodule

module four_bit_full_adder_without_enable (
  input  a0,
  input  b0,
  input  carry_in,
  input  a1,
  input  b1,
  input  a2,
  input  b2,
  input  a3,
  input  b3,
  output s0,
  output s1,
  output s2,
  output s3,
  output carry_out
);

  wire one_bit_full_adder_1_carry_out, one_bit_full_adder_2_carry_out, one_bit_full_adder_3_carry_out;

  one_bit_full_adder one_bit_full_adder_1 (
    .a(a0), .b(b0), .carry_in(carry_in), .s(s0), .carry_out(one_bit_full_adder_1_carry_out));
  one_bit_full_adder one_bit_full_adder_2 (
    .a(a1), .b(b1), .carry_in(one_bit_full_adder_1_carry_out), .s(s1),
    .carry_out(one_bit_full_adder_2_carry_out));
  one_bit_full_adder one_bit_full_adder_3 (
    .a(a2), .b(b2), .carry_in(one_bit_full_adder_2_carry_out), .s(s2),
    .carry_out(one_bit_full_adder_3_carry_out));
  one_bit_full_adder one_bit_full_adder_4 (
    .a(a3), .b(b3), .carry_in(one_bit_full_adder_3_carry_out), .s(s3), .carry_out(carry_out));
endmodule

module main_2 (
  input  carry_in
);

  wire and_1_out, and_2_out, and_3_out, and_4_out, and_5_out, and_6_out, and_7_out, controlled_buffer_1_out,
       controlled_buffer_2_out, controlled_buffer_3_out, controlled_buffer_4_out, decoder_1_out0,
       decoder_1_out1, decoder_1_out2, decoder_1_out3, decoder_2_out0, decoder_2_out1, decoder_2_out2,
       decoder_2_out3, decoder_2_out4, decoder_2_out5, decoder_2_out6, decoder_2_out7,
       four_bit_full_adder_1_carry_out, input_a_p1, input_a_p2, input_a_p3, input_a_p4, input_b_p1,
       input_b_p2, input_b_p3, input_b_p4, multiplier_four_bit_1_s4, multiplier_four_bit_1_s5,
       multiplier_four_bit_1_s6, multiplier_four_bit_1_s7, or_1_out;
  wire [1:0] screen_p2;
  wire [2:0] opcode_p3;
  wire [3:0] double_dabble_1_h0, double_dabble_1_o0, double_dabble_1_t0;

  // DipSwitch #(.number(2)) screen: pin names not known; wires that end beside it: screen_p2[1], screen_p2[0]
  Decoder #(.enable("false"), .select(2)) decoder_1 (
    .out0(decoder_1_out0), .out1(decoder_1_out1), .out2(decoder_1_out2), .out3(decoder_1_out3),
    .sel(screen_p2));
  // DipSwitch #(.number(3)) opcode: pin names not known; wires that end beside it: opcode_p3[2], opcode_p3[1], opcode_p3[0]
  Decoder #(.enable("false"), .select(3)) decoder_2 (
    .out0(decoder_2_out0), .out1(decoder_2_out1), .out2(decoder_2_out2), .out3(decoder_2_out3),
    .out4(decoder_2_out4), .out5(decoder_2_out5), .out6(decoder_2_out6), .out7(decoder_2_out7),
    .sel(opcode_p3));
  LED error (.in(or_1_out));
  or or_1 (or_1_out, decoder_2_out7, decoder_2_out6);
  assign controlled_buffer_1_out = decoder_1_out0 ? opcode_p3[2] : 1'bz;  // Controlled_Buffer controlled_buffer_1
  assign controlled_buffer_2_out = decoder_1_out0 ? opcode_p3[1] : 1'bz;  // Controlled_Buffer controlled_buffer_2
  assign controlled_buffer_3_out = decoder_1_out0 ? opcode_p3[0] : 1'bz;  // Controlled_Buffer controlled_buffer_3
  and and_1 (and_1_out, decoder_2_out0, decoder_1_out3);
  and and_2 (and_2_out, decoder_2_out1, decoder_1_out3);
  and and_3 (and_3_out, decoder_2_out2, decoder_1_out3);
  and and_4 (and_4_out, decoder_2_out3, decoder_1_out3);
  and and_5 (and_5_out, decoder_2_out4, decoder_1_out3);
  and and_6 (and_6_out, decoder_2_out5, decoder_1_out3);
  // DipSwitch #(.number(4)) input_a: pin names not known; wires that end beside it: input_a_p1, input_a_p2, input_a_p3, input_a_p4
  assign controlled_buffer_4_out = decoder_1_out1 ? input_a_p1 : 1'bz;  // Controlled_Buffer controlled_buffer_4
  assign controlled_buffer_1_out = decoder_1_out1 ? input_a_p2 : 1'bz;  // Controlled_Buffer controlled_buffer_5
  assign controlled_buffer_2_out = decoder_1_out1 ? input_a_p3 : 1'bz;  // Controlled_Buffer controlled_buffer_6
  assign controlled_buffer_3_out = decoder_1_out1 ? input_a_p4 : 1'bz;  // Controlled_Buffer controlled_buffer_7
  // DipSwitch #(.number(4)) input_b: pin names not known; wires that end beside it: input_b_p1, input_b_p2, input_b_p3, input_b_p4
  assign controlled_buffer_4_out = decoder_1_out2 ? input_b_p1 : 1'bz;  // Controlled_Buffer controlled_buffer_8
  assign controlled_buffer_1_out = decoder_1_out2 ? input_b_p2 : 1'bz;  // Controlled_Buffer controlled_buffer_9
  assign controlled_buffer_2_out = decoder_1_out2 ? input_b_p3 : 1'bz;  // Controlled_Buffer controlled_buffer_10
  assign controlled_buffer_3_out = decoder_1_out2 ? input_b_p4 : 1'bz;  // Controlled_Buffer controlled_buffer_11
  LED led_1 (.in(carry_in));
  double_dabble double_dabble_1 (
    .a(multiplier_four_bit_1_s7), .b(multiplier_four_bit_1_s6), .c(multiplier_four_bit_1_s5),
    .d(multiplier_four_bit_1_s4), .e(controlled_buffer_4_out), .f(controlled_buffer_1_out),
    .g(controlled_buffer_2_out), .h(controlled_buffer_3_out), .h3(double_dabble_1_h0[3]),
    .h2(double_dabble_1_h0[2]), .h1(double_dabble_1_h0[1]), .h0(double_dabble_1_h0[0]),
    .t3(double_dabble_1_t0[3]), .t2(double_dabble_1_t0[2]), .t1(double_dabble_1_t0[1]),
    .t0(double_dabble_1_t0[0]), .o3(double_dabble_1_o0[3]), .o2(double_dabble_1_o0[2]),
    .o1(double_dabble_1_o0[1]), .o0(double_dabble_1_o0[0]));
  _7_Segment_Display u_7_segment_display_1 ();  // open: g, f, a, b, e, d, c, dp
  _7_Segment_Display u_7_segment_display_2 ();  // open: g, f, a, b, e, d, c, dp
  // BCD_to_7_Segment_decoder bcd_to_7_segment_decoder_1: pin names not known
  // BCD_to_7_Segment_decoder bcd_to_7_segment_decoder_2: pin names not known
  _7_Segment_Display u_7_segment_display_3 ();  // open: g, f, a, b, e, d, c, dp
  // BCD_to_7_Segment_decoder bcd_to_7_segment_decoder_3: pin names not known
  LED carry_out (.in(four_bit_full_adder_1_carry_out));
  LED overflow (.in(and_7_out));
  and and_7 (and_7_out, four_bit_full_adder_1_carry_out, and_1_out);
  four_bit_full_adder four_bit_full_adder_1 (
    .enable(and_1_out), .a0(input_a_p4), .b0(input_b_p4), .carry_in(carry_in), .a1(input_a_p3),
    .b1(input_b_p3), .a2(input_a_p2), .b2(input_b_p2), .a3(input_a_p1), .b3(input_b_p1),
    .s0(controlled_buffer_3_out), .s1(controlled_buffer_2_out), .s2(controlled_buffer_1_out),
    .s3(controlled_buffer_4_out), .carry_out(four_bit_full_adder_1_carry_out));
  four_bit_full_subtractor four_bit_full_subtractor_1 (
    .enable(and_2_out), .a0(input_a_p4), .b0(input_b_p4), .borrow_in(carry_in), .a1(input_a_p3),
    .b1(input_b_p3), .a2(input_a_p2), .b2(input_b_p2), .a3(input_a_p1), .b3(input_b_p1),
    .s0(controlled_buffer_3_out), .s1(controlled_buffer_2_out), .s2(controlled_buffer_1_out),
    .s3(controlled_buffer_4_out), .borrow_out(four_bit_full_adder_1_carry_out));
  multiplier_four_bit multiplier_four_bit_1 (
    .enable(and_3_out), .a0(input_a_p4), .a1(input_a_p3), .a2(input_a_p2), .a3(input_a_p1), .b0(input_b_p4),
    .b1(input_b_p3), .b2(input_b_p2), .b3(input_b_p1), .s0(controlled_buffer_3_out),
    .s1(controlled_buffer_2_out), .s2(controlled_buffer_1_out), .s3(controlled_buffer_4_out),
    .s4(multiplier_four_bit_1_s4), .s5(multiplier_four_bit_1_s5), .s6(multiplier_four_bit_1_s6),
    .s7(multiplier_four_bit_1_s7));
  four_bit_and four_bit_and_1 (
    .a0(input_a_p4), .enable(and_4_out), .b0(input_b_p4), .a1(input_a_p3), .b1(input_b_p3), .a2(input_a_p2),
    .b2(input_b_p2), .a3(input_a_p1), .b3(input_b_p1), .s0(controlled_buffer_3_out),
    .s1(controlled_buffer_2_out), .s2(controlled_buffer_1_out), .s3(controlled_buffer_4_out));
  four_bit_or four_bit_or_1 (
    .a0(input_a_p4), .enable(and_5_out), .b0(input_b_p4), .a1(input_a_p3), .b1(input_b_p3), .a2(input_a_p2),
    .b2(input_b_p2), .a3(input_a_p1), .b3(input_b_p1), .s0(controlled_buffer_3_out),
    .s1(controlled_buffer_2_out), .s2(controlled_buffer_1_out), .s3(controlled_buffer_4_out));
  four_bit_xor four_bit_xor_1 (
    .a0(input_a_p4), .enable(and_6_out), .b0(input_b_p4), .a1(input_a_p3), .b1(input_b_p3), .a2(input_a_p2),
    .b2(input_b_p2), .a3(input_a_p1), .b3(input_b_p1), .s0(controlled_buffer_3_out),
    .s1(controlled_buffer_2_out), .s2(controlled_buffer_1_out), .s3(controlled_buffer_4_out));
endmodule
